# Fritzing sketch Transmitter (saved by Fritzing 0.9.4)
breadboards: 1

parts:
  STM32 = STM32F103C8T6 blue mini board
  Toggle_switch = Toggle Switch [package=THT]
  1 = Thumb Joystick [package=joystick]
  Rotary_potentiometer = Rotary Potentiometer (Small) [maximum_resistance=100kΩ package=THT]
  2 = Thumb Joystick [package=joystick]
  Slide_potentiometer = SLIDER [package=slider]
  Composant1 = InvenSense MPU6050
  LoRa_Module1 = Ra-01 - LoRa Module SX1278 [part_number=SX1278]
  ANT1 = Antenna
  VCC1_4_5V = Battery
  M1 = RioRand LM2596

nets:
  N1: STM32.B12, LoRa_Module1.NSS
  N2: STM32.B13, LoRa_Module1.SCK
  N3: STM32.B14, LoRa_Module1.MISO
  N4: STM32.B15, LoRa_Module1.MOSI
  N5: STM32.A9, Toggle_switch.L1
  N6: STM32.A10, Toggle_switch.L2
  N7: STM32.A11, LoRa_Module1.DIO0
  N8: STM32.A12, LoRa_Module1.RESET
  GND: STM32.G, 1.H-, 1.V-, Rotary_potentiometer.leg1, 2.H-, 2.V-, Slide_potentiometer.A, Composant1.GND, LoRa_Module1.GND, M1.Pin_4
  3.3V: STM32.3.3V, Toggle_switch.COM, 1.SEL+, 1.V+, 1.H+, Rotary_potentiometer.leg2, 2.SEL+, 2.V+, 2.H+, Slide_potentiometer.E, Composant1.VCC, LoRa_Module1.3.3V, M1.Pin_3
  N9: STM32.A2, Rotary_potentiometer.wiper
  N10: STM32.A3, Slide_potentiometer.S
  N11: STM32.A4, 2.SEL-
  N12: STM32.A5, 1.SEL-
  N13: STM32.A6, 2.H
  N14: STM32.A7, 2.V
  N15: STM32.B0, 1.H
  N16: STM32.B1, 1.V
  N17: STM32.B10, Composant1.SCL
  N18: STM32.B11, Composant1.SDA
  N19: LoRa_Module1.ANT, ANT1.antenna_lead
  N20: VCC1_4_5V.-, M1.Pin_2
  N21: VCC1_4_5V.+, M1.Pin_1

custom parts:
  Ra-01 - LoRa Module SX1278: The Ra-01 LoRa Module featuring the SX1278 engine by Semtech. Module by AI-Thinker. Module (Ra-01) specifications from: https://www.banggood.com/Ra-01-Smart-Electronics-SX1278-LoRa-Spread-Spectrum-Wireless-Module-Ultra-Far-10KM-433M-p-1130769.html Description: Power supply: DC1.8-3.7V(3.3V) Chip: SX1278 Frequency: 433Mhz Operating temperature: -40~+85°C On Sheild Description (may vary by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
